# Fritzing sketch HW2_multi-tap_Maija (saved by Fritzing 0.9.3b)
breadboards: 1

parts:
  Part1 = RedBear-Duo
  S1 = Pushbutton [package="[THT]"]
  S2 = Pushbutton [package="[THT]"]
  S3 = Pushbutton [package="[THT]"]
  S4 = Pushbutton [package="[THT]"]
  S5 = Pushbutton [package="[THT]"]
  S6 = Pushbutton [package="[THT]"]
  S7 = Pushbutton [package="[THT]"]
  S8 = Pushbutton [package="[THT]"]
  S9 = Pushbutton [package="[THT]"]

nets:
  N1: Part1.A0, S5.Pin_1, S5.Pin_2
  N2: Part1.A1, S6.Pin_1, S6.Pin_2
  N3: Part1.A2, S7.Pin_1, S7.Pin_2
  N4: Part1.A3, S8.Pin_1, S8.Pin_2
  N5: Part1.D0, S1.Pin_1, S1.Pin_2
  N6: Part1.D1, S2.Pin_1, S2.Pin_2
  N7: Part1.D2, S3.Pin_1, S3.Pin_2
  N8: Part1.D3, S4.Pin_1, S4.Pin_2
  N9: Part1.D4, S9.Pin_1, S9.Pin_2
  N10: Part1.3V3, S1.Pin_3, S1.Pin_4, S2.Pin_3, S2.Pin_4, S3.Pin_3, S3.Pin_4, S4.Pin_3, S4.Pin_4, S5.Pin_3, S5.Pin_4, S6.Pin_3, S6.Pin_4, S7.Pin_3, S7.Pin_4, S8.Pin_3, S8.Pin_4, S9.Pin_3, S9.Pin_4

notes:
  I use PULL_DOWN resistor of the RedBear Duo board.

custom parts:
  RedBear-Duo: Duo is a thumb-size development board made to simplify the building process of Internet of Things (IoT). This part is a modification of the Particle Photon part by Brett Walach,Fabian Althaus

// code stored in the sketch: HW2_multi-tap_Maija.ino
/*
 Debounce for RedBear Duo
 Each time the input pin goes from LOW to HIGH (e.g. because of a push-button
 press), the output pin is toggled from LOW to HIGH or HIGH to LOW.  There's
 a minimum delay between toggles to debounce the circuit (i.e. to ignore
 noise).
 The circuit:
 * internal LED on D7
 * pushbutton attached from D0 to +3V3 (uses internal pulldown)
 created 21 November 2006
 by David A. Mellis for Arduino
 modified 30 Aug 2011
 by Limor Fried
 modified 28 Dec 2012
 by Mike Walters
 modified 29 Aug 2016
 by Bjoern Hartmann for RedBear Duo
 
 This example code is in the public domain.
 http://www.arduino.cc/en/Tutorial/Debounce
 */

// do not use the cloud functions - assume programming through Arduino IDE
#if defined(ARDUINO) 
SYSTEM_MODE(MANUAL); 
#endif

// constants won't change. They're used here to
// set pin numbers:
const int button1Pin = D0;    // the number of the pushbutton pin
const int button2Pin = D1;
const int button3Pin = D2;
const int button4Pin = D3;

const int button5Pin = D4;

const int button6Pin = D8;
const int button7Pin = D9;
const int button8Pin = D10;
const int button9Pin = D11;


String hello1String = "efgh"; //strings with data for each button
int string1Pos = -1;
String hello2String = "mnop";
int string2Pos = -1;
String hello3String = "uvwx";
int string3Pos = -1;
String hello4String = " 0123456789";
int string4Pos = -1;


String hello6String = "abcd";
int string6Pos = -1;
String hello7String = "ijkl";
int string7Pos = -1;
String hello8String = "qrst";
int string8Pos = -1;
String hello9String = "yz?!";
int string9Pos = -1;




void setup() {
  pinMode(button1Pin, INPUT_PULLDOWN);
  pinMode(button2Pin, INPUT_PULLDOWN);
  pinMode(button3Pin, INPUT_PULLDOWN);
  pinMode(button4Pin, INPUT_PULLDOWN);
  
  pinMode(button5Pin, INPUT_PULLDOWN);
  
  pinMode(button6Pin, INPUT_PULLDOWN);
  pinMode(button7Pin, INPUT_PULLDOWN);
  pinMode(button8Pin, INPUT_PULLDOWN);
  pinMode(button9Pin, INPUT_PULLDOWN);

  Serial.begin(9600);


}



void loop() {
  
  
int button1State, button2State, button3State, button4State, button5State, button6State, button7State, button8State, button9State; 

button1State = digitalRead(button1Pin);
button2State = digitalRead(button2Pin);
button3State = digitalRead(button3Pin);
button4State = digitalRead(button4Pin);

button5State = digitalRead(button5Pin);

button6State = digitalRead(button6Pin);
button7State = digitalRead(button7Pin);
button8State = digitalRead(button8Pin);
button9State = digitalRead(button9Pin);



if (button1State == HIGH){    //press character button
  string1Pos++;
  delay (200);
}

  if (button5State == HIGH){  //press enter

    int current1Pos = string1Pos; 
    Serial.print(hello1String.charAt(current1Pos));
    string1Pos = -1;

 
  delay (100);

}

if (button2State == HIGH){
  string2Pos++;
  delay (200);
}

   if (button5State == HIGH){
    int current2Pos = string2Pos;
    Serial.print(hello2String.charAt(current2Pos));
    string2Pos = -1;

    delay (100);
  }

if (button3State == HIGH){
  string3Pos++;
  delay (200);
}

  if (button5State == HIGH){
    int current3Pos = string3Pos;
    Serial.print(hello3String.charAt(current3Pos));
    string3Pos = -1;

    delay (100);
  }

  if (button4State == HIGH){
  string4Pos++;
  delay (200);
}

  if (button5State == HIGH){
    int current4Pos = string4Pos;
    Serial.print(hello4String.charAt(current4Pos));
    string4Pos = -1;

    delay (100);
  }

  
if (button6State == HIGH){
  string6Pos++;
  delay (200);
}

  if (button5State == HIGH){

    int current6Pos = string6Pos; 
    Serial.print(hello6String.charAt(current6Pos));
    string6Pos = -1;

 
  delay (100);

}

if (button7State == HIGH){
  string7Pos++;
  delay (200);
}

  if (button5State == HIGH){

    int current7Pos = string7Pos; 
    Serial.print(hello7String.charAt(current7Pos));
    string7Pos = -1;

 
  delay (100);

}

if (button8State == HIGH){
  string8Pos++;
  delay (200);
}

  if (button5State == HIGH){

    int current8Pos = string8Pos; 
    Serial.print(hello8String.charAt(current8Pos));
    string8Pos = -1;

 
  delay (100);

}

if (button9State == HIGH){
  string9Pos++;
  delay (200);
}

  if (button5State == HIGH){

    int current9Pos = string9Pos; 
    Serial.print(hello9String.charAt(current9Pos));
    string9Pos = -1;

 
  delay (100);

}
  

}
